// Digital circuit CPU.dig as structural Verilog
module CPU (
  input  CLK,
  input  RegF_WE,
  input  [3:0] BranchLine,
  input  GoBranch
);

  wire counterpreset_1_ovf, IMM_check, Use_ALU;
  wire [1:0] Do_Math;
  wire [3:0] counterpreset_1_out;
  wire [7:0] ALU_output, DataA, DataB, Instruction_d, RegFile_db;
  wire [17:8] Instruction_d_2;

  CounterPreset #(.Bits(4)) counterpreset_1 (
    .en(1'b1), .C(CLK), .dir(1'b0), .in(BranchLine), .ld(GoBranch), .clr(counterpreset_1_ovf),
    .out(counterpreset_1_out), .ovf(counterpreset_1_ovf));
  ROM #(.AddrBits(4), .Bits(19)) Instruction (
    .A(counterpreset_1_out), .sel(1'b1), .D({IMM_check, Instruction_d_2, Instruction_d}));
  ROM #(.AddrBits(4), .Bits(3)) CU (.A(Instruction_d_2[17:14]), .sel(1'b1), .D({Use_ALU, Do_Math}));
  RegisterFile #(.AddrBits(3), .Bits(8)) RegFile (
    .Din(ALU_output), .we(RegF_WE), .Rw(Instruction_d_2[13:11]), .C(CLK), .Ra(Instruction_d_2[10:8]),
    .Rb(Instruction_d[2:0]), .Da(DataA), .Db(RegFile_db));
  // ALU ALU: pin names not known; wires that end beside it: DataA, DataB, Do_Math, Use_ALU, ALU_output
  Multiplexer #(.Bits(8)) multiplexer_1 (.sel(IMM_check), .in_0(RegFile_db), .in_1(Instruction_d), .out(DataB));

  // Other names for the same wires on the sheet: Go_Branch = GoBranch; Line_Branch[3:0] = BranchLine

  // Notes on the sheet:
  //   RegF_WE: default 1
  //   contents of Instruction (hex, n*v repeats v):
  //   40a0f,4103f,5a01
  //   contents of CU (hex, n*v repeats v):
  //   4,5
endmodule
